# Fritzing sketch Kaddu_Klock (saved by Fritzing 0.6.3b)
breadboards: 2

parts:
  Arduino1 = Arduino
  DI1 = 7-Segment LED Display [package=THT]
  DI2 = 7-Segment LED Display [package=THT]
  U1 = 74HC595 [package="DIP16 [THT]"]

nets:
  GND: Arduino1.GND, DI1.commAnode#2, DI2.commAnode#2, U1.GND
